// Logisim project Laboratorio2.circ as structural Verilog: 3 circuits, main circuit main
module main (
  input  [6:0] in_1
);

  wire a, a1, b, b1, bcd7segx2_1_dmax, bcd7segx2_1_dmin, bcd7segx2_1_out_3, bcd7segx2_1_out_4,
       bcd7segx2_1_out_7, bcd7segx2_1_out_8, bcd7segx2_1_umax, bcd7segx2_1_umin, c, c1, d, d1, e, e1, f, f1,
       g, g1;

  _7_Segment_Display u_7_segment_display_1 (.g(g), .f(f), .a(a), .b(b), .e(e), .d(d), .c(c));  // open: dp
  _7_Segment_Display u_7_segment_display_2 (.g(g1), .f(f1), .a(a1), .b(b1), .e(e1), .d(d1), .c(c1));  // open: dp
  BCD7SEGx2 bcd7segx2_1 (
    .in_1(in_1), .dmin(bcd7segx2_1_dmin), .out_3(bcd7segx2_1_out_3), .out_4(bcd7segx2_1_out_4),
    .dmax(bcd7segx2_1_dmax), .umin(bcd7segx2_1_umin), .out_7(bcd7segx2_1_out_7), .out_8(bcd7segx2_1_out_8),
    .umax(bcd7segx2_1_umax));
  BCD7SEG Decenas (
    .min(bcd7segx2_1_dmin), .in_2(bcd7segx2_1_out_3), .in_3(bcd7segx2_1_out_4), .max(bcd7segx2_1_dmax),
    .a(a), .b(b), .c(c), .d(d), .e(e), .f(f), .g(g));
  BCD7SEG Unidades (
    .min(bcd7segx2_1_umin), .in_2(bcd7segx2_1_out_7), .in_3(bcd7segx2_1_out_8), .max(bcd7segx2_1_umax),
    .a(a1), .b(b1), .c(c1), .d(d1), .e(e1), .f(f1), .g(g1));
endmodule

module BCD7SEG (
  input  min,
  input  in_2,
  input  in_3,
  input  max,
  output a,
  output b,
  output c,
  output d,
  output e,
  output f,
  output g
);

  wire and_1_out, and_2_out, and_3_out, and_4_out, and_5_out, and_6_out, and_7_out, and_8_out, and_9_out,
       and_10_out, and_11_out, and_12_out, and_13_out, and_14_out, and_15_out, and_16_out, and_17_out,
       and_18_out, and_19_out, and_20_out, and_21_out, and_22_out, and_23_out, and_24_out, and_25_out,
       not_1_out, not_2_out, not_3_out, not_4_out;

  not not_1 (not_1_out, max);
  not not_2 (not_2_out, in_3);
  not not_3 (not_3_out, in_2);
  not not_4 (not_4_out, min);
  and and_1 (and_1_out, not_1_out, not_2_out, not_4_out);
  and and_2 (and_2_out, not_1_out, in_2);
  and and_3 (and_3_out, not_1_out, in_3, min);
  and and_4 (and_4_out, max, not_2_out, not_3_out);
  and and_5 (and_5_out, not_1_out, not_2_out);
  and and_6 (and_6_out, not_1_out, not_3_out, not_4_out);
  and and_7 (and_7_out, not_2_out, not_3_out);
  and and_8 (and_8_out, not_1_out, in_2, min);
  and and_9 (and_9_out, not_2_out, not_3_out);
  and and_10 (and_10_out, not_1_out, min);
  and and_11 (and_11_out, not_1_out, in_3);
  and and_12 (and_12_out, not_2_out, not_3_out, not_4_out);
  and and_13 (and_13_out, not_1_out, not_2_out, in_2);
  and and_14 (and_14_out, not_1_out, in_2, not_4_out);
  and and_15 (and_15_out, not_1_out, in_3, not_3_out, min);
  and and_16 (and_16_out, not_2_out, not_3_out, not_4_out);
  and and_17 (and_17_out, not_1_out, in_2, not_4_out);
  and and_18 (and_18_out, not_1_out, not_3_out, not_4_out);
  and and_19 (and_19_out, not_1_out, in_3, not_3_out);
  and and_20 (and_20_out, not_1_out, in_3, not_4_out);
  and and_21 (and_21_out, max, not_2_out, not_3_out);
  and and_22 (and_22_out, not_1_out, not_2_out, in_2);
  and and_23 (and_23_out, not_1_out, in_3, not_3_out);
  and and_24 (and_24_out, not_1_out, in_3, not_4_out);
  and and_25 (and_25_out, max, not_2_out, not_3_out);
  or or_1 (a, and_1_out, and_2_out, and_3_out, and_4_out);
  or or_2 (b, and_5_out, and_6_out, and_7_out, and_8_out);
  or or_3 (c, and_9_out, and_10_out, and_11_out);
  or or_4 (d, and_12_out, and_13_out, and_14_out, and_15_out);
  or or_5 (e, and_16_out, and_17_out);
  or or_6 (f, and_18_out, and_19_out, and_20_out, and_21_out);
  or or_7 (g, and_22_out, and_23_out, and_24_out, and_25_out);
endmodule

module BCD7SEGx2 (
  input  [6:0] in_1,
  output dmin,
  output out_3,
  output out_4,
  output dmax,
  output umin,
  output out_7,
  output out_8,
  output umax
);

  wire [6:4] divider_1_out, divider_1_rem;

  Divider #(.width(7)) divider_1 (
    .a(in_1), .b(7'b0001010), .out({divider_1_out, dmax, out_4, out_3, dmin}),
    .rem({divider_1_rem, umax, out_8, out_7, umin}));  // open: upper
  // Probe on {divider_1_rem, umax, out_8, out_7, umin}
  // Probe on {divider_1_out, dmax, out_4, out_3, dmin}
endmodule
